# Fritzing sketch sketch (saved by Fritzing 0.9.5d)

parts:
  WeMos_D1_Mini1 = WeMos D1 Mini
  U1 = LIPO-1000mAh [package=lipo-1000]
  HC-SR04_Sensor_1 = HC-SR04 Ultrasonic Distance Sensor

nets:
  N1: WeMos_D1_Mini1.5V, U1.+
  N2: WeMos_D1_Mini1.D5, HC-SR04_Sensor_1.ECHO
  N3: WeMos_D1_Mini1.D6, HC-SR04_Sensor_1.TRIG
  N4: WeMos_D1_Mini1.D8, HC-SR04_Sensor_1.VCC
  N5: WeMos_D1_Mini1.G, U1.-, HC-SR04_Sensor_1.GND
